// Digital circuit main.dig as structural Verilog
module main (
  input  A,
  input  B,
  input  C,
  output Sum,
  output Carry
);

  Full_Adder full_adder_1 (.A(A), .B(B), .C(C), .Sum(Sum), .Carry(Carry));

  // Notes on the sheet:
  //   A: pin V17
  //   B: pin V16
  //   C: pin W16
  //   Sum: pin U16
  //   Carry: pin E19
endmodule
