// Digital circuit 3and.dig as structural Verilog
module _3and (
  input  _1,
  input  _2,
  input  _3,
  output S
);

  wire and_1_out;

  and and_1 (and_1_out, _1, _2);
  and and_2 (S, and_1_out, _3);
endmodule
