// Digital circuit 3or.dig as structural Verilog
module _3or (
  input  _1,
  input  _2,
  input  _3,
  output S
);

  wire or_1_out;

  or or_1 (or_1_out, _1, _2);
  or or_2 (S, or_1_out, _3);
endmodule
