// Digital circuit 4and.dig as structural Verilog
module _4and (
  input  _1,
  input  _2,
  input  _3,
  input  _4,
  output S
);

  wire and_1_out, and_2_out;

  and and_1 (and_1_out, _1, _2);
  and and_2 (and_2_out, _3, _4);
  and and_3 (S, and_1_out, and_2_out);
endmodule
