// Digital circuit CA.dig as structural Verilog
module CA (
  input  B3,
  input  B2,
  input  B1,
  input  B0,
  output CA
);

  wire nor_1_out, xor_1_out;

  nor nor_1 (nor_1_out, B3, B1);
  xor xor_1 (xor_1_out, B2, B0);
  and and_1 (CA, nor_1_out, xor_1_out);
endmodule
