// Digital circuit CB.dig as structural Verilog
module CB (
  input  B3,
  input  B2,
  input  B1,
  input  B0,
  output CB
);

  wire and_1_out, not_1_out, xor_1_out;

  not not_1 (not_1_out, B3);
  and and_1 (and_1_out, not_1_out, B2);
  xor xor_1 (xor_1_out, B1, B0);
  and and_2 (CB, and_1_out, xor_1_out);
endmodule
