// Digital circuit CC.dig as structural Verilog
module CC (
  input  B3,
  input  B2,
  input  B1,
  input  B0,
  output CC
);

  wire and_1_out, nor_1_out, not_1_out;

  not not_1 (not_1_out, B0);
  nor nor_1 (nor_1_out, B3, B2);
  and and_1 (and_1_out, B1, not_1_out);
  and and_2 (CC, nor_1_out, and_1_out);
endmodule
