// Digital circuit CD.dig as structural Verilog
module CD (
  input  B3,
  input  B2,
  input  B1,
  input  B0,
  output CD
);

  wire and_1_out, and_2_out, nor_1_out, not_1_out, or_1_out, xnor_1_out;

  not not_1 (not_1_out, B3);
  xnor xnor_1 (xnor_1_out, B1, B0);
  nor nor_1 (nor_1_out, B2, B1);
  and and_1 (and_1_out, B2, xnor_1_out);
  and and_2 (and_2_out, nor_1_out, B0);
  or or_1 (or_1_out, and_1_out, and_2_out);
  and and_3 (CD, not_1_out, or_1_out);
endmodule
