// Digital circuit lab2_SSD_driver.dig as structural Verilog
module lab2_SSD_driver (
  input  B0,
  input  B1,
  input  B2,
  input  B3,
  output CC,
  output CD,
  output CE,
  output CF,
  output CG,
  output CB,
  output CA
);

  lab2_driver_a lab2_driver_a_1 (.B4(B0), .B5(B1), .B6(B2), .B7(B3), .CA(CA));
  lab2_driver_b lab2_driver_b_1 (.B0(B0), .B1(B1), .B2(B2), .B3(B3), .CB(CB));
  lab2_driver_c lab2_driver_c_1 (.B0(B0), .B1(B1), .B2(B2), .B3(B3), .CC(CC));
  lab2_driver_d lab2_driver_d_1 (.B0(B0), .B1(B1), .B2(B2), .B3(B3), .CD(CD));
  lab2_driver_e lab2_driver_e_1 (.B0(B0), .B1(B1), .B2(B2), .B3(B3), .CE(CE));
  lab2_driver_f lab2_driver_f_1 (.B0(B0), .B1(B1), .B2(B2), .B3(B3), .CF(CF));
  lab2_driver_g lab2_driver_g_1 (.B0(B0), .B1(B1), .B2(B2), .B3(B3), .CF(CG));
endmodule
