// Digital circuit lab2_driver_a.dig as structural Verilog
module lab2_driver_a (
  input  B4,
  input  B5,
  input  B6,
  input  B7,
  output CA
);

  wire _4and_1_s, _4and_2_s, not_1_out, not_2_out, not_3_out, not_4_out, not_5_out, not_6_out, or_1_out;

  not not_1 (not_1_out, B5);
  not not_2 (not_2_out, B6);
  not not_3 (not_3_out, B7);
  not not_4 (not_4_out, B4);
  not not_5 (not_5_out, B5);
  not not_6 (not_6_out, B7);
  _4and _4and_1 (._1(B4), ._2(not_1_out), ._3(not_2_out), ._4(not_3_out), .S(_4and_1_s));
  _4and _4and_2 (._1(not_4_out), ._2(not_5_out), ._3(B6), ._4(not_6_out), .S(_4and_2_s));
  or or_1 (or_1_out, _4and_1_s, _4and_2_s);
  not not_7 (CA, or_1_out);
endmodule
