// Digital circuit lab2_driver_b.dig as structural Verilog
module lab2_driver_b (
  input  B0,
  input  B1,
  input  B2,
  input  B3,
  output CB
);

  wire _3and_1_s, and_1_out, and_2_out, not_1_out, not_2_out, not_3_out, or_1_out;

  not not_1 (not_1_out, B1);
  and and_1 (and_1_out, not_1_out, B0);
  not not_2 (not_2_out, B0);
  and and_2 (and_2_out, not_2_out, B1);
  not not_3 (not_3_out, B3);
  or or_1 (or_1_out, and_1_out, and_2_out);
  _3and _3and_1 (._1(or_1_out), ._2(B2), ._3(not_3_out), .S(_3and_1_s));
  not not_4 (CB, _3and_1_s);
endmodule
