// Digital circuit lab2_driver_c.dig as structural Verilog
module lab2_driver_c (
  input  B0,
  input  B1,
  input  B2,
  input  B3,
  output CC
);

  wire _4and_1_s, not_1_out, not_2_out, not_3_out;

  not not_1 (not_1_out, B0);
  not not_2 (not_2_out, B2);
  not not_3 (not_3_out, B3);
  _4and _4and_1 (._1(not_1_out), ._2(B1), ._3(not_2_out), ._4(not_3_out), .S(_4and_1_s));
  not not_4 (CC, _4and_1_s);
endmodule
