// Digital circuit lab2_driver_d.dig as structural Verilog
module lab2_driver_d (
  input  B0,
  input  B1,
  input  B2,
  input  B3,
  output CD
);

  wire _3or_1_s, _4and_1_s, _4and_2_s, _4and_3_s, not_1_out, not_2_out, not_3_out, not_4_out, not_5_out,
       not_6_out, not_7_out;

  not not_1 (not_1_out, B1);
  not not_2 (not_2_out, B2);
  not not_3 (not_3_out, B3);
  not not_4 (not_4_out, B0);
  not not_5 (not_5_out, B1);
  not not_6 (not_6_out, B3);
  not not_7 (not_7_out, B3);
  _4and _4and_1 (._1(B0), ._2(not_1_out), ._3(not_2_out), ._4(not_3_out), .S(_4and_1_s));
  _4and _4and_2 (._1(not_4_out), ._2(not_5_out), ._3(B2), ._4(not_6_out), .S(_4and_2_s));
  _4and _4and_3 (._1(B0), ._2(B1), ._3(B2), ._4(not_7_out), .S(_4and_3_s));
  _3or _3or_1 (._1(_4and_1_s), ._2(_4and_2_s), ._3(_4and_3_s), .S(_3or_1_s));
  not not_8 (CD, _3or_1_s);
endmodule
