// Digital circuit lab2_driver_e.dig as structural Verilog
module lab2_driver_e (
  input  B0,
  input  B1,
  input  B2,
  input  B3,
  output CE
);

  wire _3and_1_s, _3and_2_s, _3and_3_s, _3or_1_s, and_1_out, and_2_out, and_3_out, and_4_out, not_1_out,
       not_2_out, not_3_out, not_4_out, not_5_out, not_6_out, not_7_out, not_8_out, not_9_out, not_10_out;

  not not_1 (not_1_out, B0);
  not not_2 (not_2_out, B2);
  not not_3 (not_3_out, B3);
  not not_4 (not_4_out, B3);
  not not_5 (not_5_out, B1);
  not not_6 (not_6_out, B2);
  not not_7 (not_7_out, B1);
  not not_8 (not_8_out, B0);
  not not_9 (not_9_out, B2);
  not not_10 (not_10_out, B3);
  _3and _3and_1 (._1(B1), ._2(not_2_out), ._3(not_3_out), .S(_3and_1_s));
  _3and _3and_2 (._1(B1), ._2(B2), ._3(not_4_out), .S(_3and_2_s));
  _3and _3and_3 (._1(not_5_out), ._2(not_6_out), ._3(B3), .S(_3and_3_s));
  and and_1 (and_1_out, not_7_out, not_9_out);
  and and_2 (and_2_out, not_8_out, not_10_out);
  and and_3 (and_3_out, and_1_out, and_2_out);
  _3or _3or_1 (._1(_3and_1_s), ._2(_3and_2_s), ._3(_3and_3_s), .S(_3or_1_s));
  and and_4 (and_4_out, not_1_out, _3or_1_s);
  or or_1 (CE, and_4_out, and_3_out);
endmodule
