// Digital circuit lab2_driver_f.dig as structural Verilog
module lab2_driver_f (
  input  B0,
  input  B1,
  input  B2,
  input  B3,
  output CF
);

  wire _3and_1_s, and_1_out, and_2_out, and_3_out, and_4_out, and_5_out, not_1_out, not_2_out, not_3_out,
       not_4_out, not_5_out, not_6_out, or_1_out;

  not not_1 (not_1_out, B3);
  not not_2 (not_2_out, B0);
  not not_3 (not_3_out, B2);
  not not_4 (not_4_out, B1);
  not not_5 (not_5_out, B3);
  and and_1 (and_1_out, B2, not_1_out);
  _3and _3and_1 (._1(B0), ._2(B1), ._3(B2), .S(_3and_1_s));
  not not_6 (not_6_out, _3and_1_s);
  and and_2 (and_2_out, not_2_out, not_4_out);
  and and_3 (and_3_out, not_3_out, not_5_out);
  and and_4 (and_4_out, not_6_out, and_1_out);
  and and_5 (and_5_out, and_2_out, and_3_out);
  or or_1 (or_1_out, and_4_out, B3);
  or or_2 (CF, or_1_out, and_5_out);
endmodule
