// Digital circuit lab2_driver_g.dig as structural Verilog
module lab2_driver_g (
  input  B0,
  input  B1,
  input  B2,
  input  B3,
  output CF
);

  wire _3and_1_s, and_1_out, and_2_out, and_3_out, not_1_out, not_2_out, not_3_out;

  not not_1 (not_1_out, B1);
  not not_2 (not_2_out, B2);
  not not_3 (not_3_out, B3);
  and and_1 (and_1_out, 1'b1, not_2_out);
  and and_2 (and_2_out, not_1_out, not_3_out);
  _3and _3and_1 (._1(B0), ._2(B1), ._3(B2), .S(_3and_1_s));
  and and_3 (and_3_out, and_1_out, and_2_out);
  nor nor_1 (CF, and_3_out, _3and_1_s);
endmodule
