// Digital circuit main.dig as structural Verilog
module main (
  input  B0,
  input  B1,
  input  B2,
  input  B3,
  input  _0,
  input  _1,
  input  _2,
  input  _3,
  output CC,
  output CD,
  output CE,
  output CF,
  output CG,
  output CB,
  output CA,
  output AN0,
  output AN1,
  output AN2,
  output AN3
);

  wire lab2_ssd_driver_1_ca, lab2_ssd_driver_1_cb, lab2_ssd_driver_1_cc, lab2_ssd_driver_1_cd,
       lab2_ssd_driver_1_ce, lab2_ssd_driver_1_cf, lab2_ssd_driver_1_cg;

  lab2_SSD_driver lab2_ssd_driver_1 (
    .B0(B0), .B1(B1), .B2(B2), .B3(B3), .CC(lab2_ssd_driver_1_cc), .CD(lab2_ssd_driver_1_cd),
    .CE(lab2_ssd_driver_1_ce), .CF(lab2_ssd_driver_1_cf), .CG(lab2_ssd_driver_1_cg),
    .CB(lab2_ssd_driver_1_cb), .CA(lab2_ssd_driver_1_ca));
  not not_1 (CC, lab2_ssd_driver_1_cc);
  not not_2 (CD, lab2_ssd_driver_1_cd);
  not not_3 (CE, lab2_ssd_driver_1_ce);
  not not_4 (CF, lab2_ssd_driver_1_cf);
  not not_5 (CG, lab2_ssd_driver_1_cg);
  not not_6 (CB, lab2_ssd_driver_1_cb);
  not not_7 (CA, lab2_ssd_driver_1_ca);

  assign AN0 = _0;
  assign AN1 = _1;
  assign AN2 = _2;
  assign AN3 = _3;

  // Notes on the sheet:
  //   B0: pin V17
  //   B1: pin V16
  //   B2: pin W16
  //   B3: pin W17
  //   CC: pin U8
  //   CD: pin V8
  //   CE: pin U5
  //   CF: pin V5
  //   CG: pin U7
  //   CB: pin W6
  //   CA: pin W7
  //   _0: pin W15
  //   AN0: pin U2
  //   _1: pin V15
  //   AN1: pin U4
  //   _2: pin W14
  //   AN2: pin V4
  //   _3: pin W13
  //   AN3: pin W4
endmodule
