// Digital circuit 4b-add.dig as structural Verilog
module _4b_add (
  input  a3,
  input  a2,
  input  a1,
  input  a0,
  input  b3,
  input  b2,
  input  b1,
  input  b0,
  output S3,
  output S2,
  output S1,
  output S0,
  output Cout
);

  wire add_1_c_o, add_2_c_o, add_3_c_o;

  Add add_1 (.a(a0), .b(b0), .c_i(1'b0), .s(S0), .c_o(add_1_c_o));
  Add add_2 (.a(a1), .b(b1), .c_i(add_1_c_o), .s(S1), .c_o(add_2_c_o));
  Add add_3 (.a(a2), .b(b2), .c_i(add_2_c_o), .s(S2), .c_o(add_3_c_o));
  Add add_4 (.a(a3), .b(b3), .c_i(add_3_c_o), .s(S3), .c_o(Cout));
endmodule
