// Digital circuit 4b-and.dig as structural Verilog
module _4b_and (
  input  a3,
  input  a2,
  input  a1,
  input  a0,
  input  b3,
  input  b2,
  input  b1,
  input  b0,
  output S3,
  output S2,
  output S1,
  output S0,
  output Cout
);

  and and_1 (S0, a0, b0);
  and and_2 (S1, a1, b1);
  and and_3 (S2, a2, b2);
  and and_4 (S3, a3, b3);

  assign Cout = 1'b0;
endmodule
