// Digital circuit 4b-or.dig as structural Verilog
module _4b_or (
  input  a3,
  input  a2,
  input  a1,
  input  a0,
  input  b3,
  input  b2,
  input  b1,
  input  b0,
  output S3,
  output S2,
  output S1,
  output S0,
  output Cout
);

  or or_1 (S0, a0, b0);
  or or_2 (S1, a1, b1);
  or or_3 (S2, a2, b2);
  or or_4 (S3, a3, b3);

  assign Cout = 1'b0;
endmodule
