// Digital circuit 4b-sub.dig as structural Verilog
module _4b_sub (
  input  a3,
  input  a2,
  input  a1,
  input  a0,
  input  b3,
  input  b2,
  input  b1,
  input  b0,
  output S3,
  output S2,
  output S1,
  output S0,
  output Cout
);

  wire add_1_c_o, add_2_c_o, add_3_c_o, not_1_out, not_2_out, not_3_out, not_4_out;

  not not_1 (not_1_out, b0);
  Add add_1 (.a(a0), .b(not_1_out), .c_i(1'b1), .s(S0), .c_o(add_1_c_o));
  Add add_2 (.a(a1), .b(not_2_out), .c_i(add_1_c_o), .s(S1), .c_o(add_2_c_o));
  not not_2 (not_2_out, b1);
  not not_3 (not_3_out, b2);
  Add add_3 (.a(a2), .b(not_3_out), .c_i(add_2_c_o), .s(S2), .c_o(add_3_c_o));
  not not_4 (not_4_out, b3);
  Add add_4 (.a(a3), .b(not_4_out), .c_i(add_3_c_o), .s(S3), .c_o(Cout));
endmodule
