// Digital circuit main.dig as structural Verilog
module main (
  input  a3,
  input  b3,
  input  a2,
  input  b2,
  input  a1,
  input  b1,
  input  a0,
  input  b0,
  input  s1,
  input  s0,
  output out0,
  output out1,
  output out2,
  output out3,
  output outc
);

  wire _4b_add_1_cout, _4b_add_1_s0, _4b_add_1_s1, _4b_add_1_s2, _4b_add_1_s3, _4b_and_1_cout, _4b_and_1_s0,
       _4b_and_1_s1, _4b_and_1_s2, _4b_and_1_s3, _4b_or_1_cout, _4b_or_1_s0, _4b_or_1_s1, _4b_or_1_s2,
       _4b_or_1_s3, _4b_sub_1_cout, _4b_sub_1_s0, _4b_sub_1_s1, _4b_sub_1_s2, _4b_sub_1_s3;

  _4b_or _4b_or_1 (
    .a3(a3), .a2(a2), .a1(a1), .a0(a0), .b3(b3), .b2(b2), .b1(b1), .b0(b0), .S3(_4b_or_1_s3),
    .S2(_4b_or_1_s2), .S1(_4b_or_1_s1), .S0(_4b_or_1_s0), .Cout(_4b_or_1_cout));
  _4b_and _4b_and_1 (
    .a3(a3), .a2(a2), .a1(a1), .a0(a0), .b3(b3), .b2(b2), .b1(b1), .b0(b0), .S3(_4b_and_1_s3),
    .S2(_4b_and_1_s2), .S1(_4b_and_1_s1), .S0(_4b_and_1_s0), .Cout(_4b_and_1_cout));
  _4b_sub _4b_sub_1 (
    .a3(a3), .a2(a2), .a1(a1), .a0(a0), .b3(b3), .b2(b2), .b1(b1), .b0(b0), .S3(_4b_sub_1_s3),
    .S2(_4b_sub_1_s2), .S1(_4b_sub_1_s1), .S0(_4b_sub_1_s0), .Cout(_4b_sub_1_cout));
  _4b_add _4b_add_1 (
    .a3(a3), .a2(a2), .a1(a1), .a0(a0), .b3(b3), .b2(b2), .b1(b1), .b0(b0), .S3(_4b_add_1_s3),
    .S2(_4b_add_1_s2), .S1(_4b_add_1_s1), .S0(_4b_add_1_s0), .Cout(_4b_add_1_cout));
  mux5b4x1 mux5b4x1_1 (
    .a3(_4b_add_1_s3), .b3(_4b_sub_1_s3), .a2(_4b_add_1_s2), .b2(_4b_sub_1_s2), .a1(_4b_add_1_s1),
    .b1(_4b_sub_1_s1), .a0(_4b_add_1_s0), .b0(_4b_sub_1_s0), .s1(s1), .c3(_4b_and_1_s3), .d3(_4b_or_1_s3),
    .c2(_4b_and_1_s2), .d2(_4b_or_1_s2), .c1(_4b_and_1_s1), .d1(_4b_or_1_s1), .c0(_4b_and_1_s0),
    .d0(_4b_or_1_s0), .s0(s0), .ac(_4b_add_1_cout), .bc(_4b_sub_1_cout), .cc(_4b_and_1_cout),
    .dc(_4b_or_1_cout), .out1(out1), .out2(out2), .out3(out3), .out0(out0), .outc(outc));

  // Notes on the sheet:
  //   a3: pin W13
  //   b3: pin W17
  //   a2: pin W14
  //   b2: pin W16
  //   a1: pin V15
  //   b1: pin V16
  //   a0: pin W15
  //   b0: pin V17
  //   s1: pin T18
  //   s0: pin U17
  //   out0: pin U16
  //   out1: pin E19
  //   out2: pin U19
  //   out3: pin V19
  //   outc: pin W18
endmodule
