// Digital circuit mux1b2x1.dig as structural Verilog
module mux1b2x1 (
  input  a,
  input  b,
  input  s,
  output Out
);

  wire and_1_out, and_2_out, not_1_out;

  not not_1 (not_1_out, s);
  and and_1 (and_1_out, a, not_1_out);
  and and_2 (and_2_out, b, s);
  or or_1 (Out, and_1_out, and_2_out);
endmodule
