// Digital circuit mux5b2x1.dig as structural Verilog
module mux5b2x1 (
  input  a3,
  input  b3,
  input  a2,
  input  b2,
  input  a1,
  input  b1,
  input  a0,
  input  b0,
  input  s,
  input  ac,
  input  bc,
  output out3,
  output out2,
  output out1,
  output out0,
  output outc
);

  mux1b2x1 mux1b2x1_1 (.a(ac), .b(bc), .s(s), .Out(outc));
  mux1b2x1 mux1b2x1_2 (.a(a3), .b(b3), .s(s), .Out(out3));
  mux1b2x1 mux1b2x1_3 (.a(a2), .b(b2), .s(s), .Out(out2));
  mux1b2x1 mux1b2x1_4 (.a(a1), .b(b1), .s(s), .Out(out1));
  mux1b2x1 mux1b2x1_5 (.a(a0), .b(b0), .s(s), .Out(out0));
endmodule
