// Digital circuit mux5b4x1.dig as structural Verilog
module mux5b4x1 (
  input  a3,
  input  b3,
  input  a2,
  input  b2,
  input  a1,
  input  b1,
  input  a0,
  input  b0,
  input  s1,
  input  c3,
  input  d3,
  input  c2,
  input  d2,
  input  c1,
  input  d1,
  input  c0,
  input  d0,
  input  s0,
  input  ac,
  input  bc,
  input  cc,
  input  dc,
  output out1,
  output out2,
  output out3,
  output out0,
  output outc
);

  wire mux5b4x2_1_outa0, mux5b4x2_1_outa1, mux5b4x2_1_outa2, mux5b4x2_1_outa3, mux5b4x2_1_outac,
       mux5b4x2_1_outb0, mux5b4x2_1_outb1, mux5b4x2_1_outb2, mux5b4x2_1_outb3, mux5b4x2_1_outbc;

  mux5b4x2 mux5b4x2_1 (
    .a3(a3), .b3(b3), .a2(a2), .b2(b2), .a1(a1), .b1(b1), .a0(a0), .b0(b0), .c3(c3), .d3(d3), .c2(c2),
    .d2(d2), .c1(c1), .d1(d1), .c0(c0), .d0(d0), .s(s0), .ac(ac), .bc(bc), .cc(cc), .dc(dc),
    .outa3(mux5b4x2_1_outa3), .outa2(mux5b4x2_1_outa2), .outa1(mux5b4x2_1_outa1), .outa0(mux5b4x2_1_outa0),
    .outb3(mux5b4x2_1_outb3), .outb2(mux5b4x2_1_outb2), .outb1(mux5b4x2_1_outb1), .outb0(mux5b4x2_1_outb0),
    .outac(mux5b4x2_1_outac), .outbc(mux5b4x2_1_outbc));
  mux5b2x1 mux5b2x1_1 (
    .a3(mux5b4x2_1_outa3), .b3(mux5b4x2_1_outb3), .a2(mux5b4x2_1_outa2), .b2(mux5b4x2_1_outb2),
    .a1(mux5b4x2_1_outa1), .b1(mux5b4x2_1_outb1), .a0(mux5b4x2_1_outa0), .b0(mux5b4x2_1_outb0), .s(s1),
    .ac(mux5b4x2_1_outac), .bc(mux5b4x2_1_outbc), .out3(out3), .out2(out2), .out1(out1), .out0(out0),
    .outc(outc));
endmodule
