// Digital circuit mux5b4x2.dig as structural Verilog
module mux5b4x2 (
  input  a3,
  input  b3,
  input  a2,
  input  b2,
  input  a1,
  input  b1,
  input  a0,
  input  b0,
  input  c3,
  input  d3,
  input  c2,
  input  d2,
  input  c1,
  input  d1,
  input  c0,
  input  d0,
  input  s,
  input  ac,
  input  bc,
  input  cc,
  input  dc,
  output outa3,
  output outa2,
  output outa1,
  output outa0,
  output outb3,
  output outb2,
  output outb1,
  output outb0,
  output outac,
  output outbc
);

  mux1b2x1 mux1b2x1_1 (.a(ac), .b(bc), .s(s), .Out(outac));
  mux1b2x1 mux1b2x1_2 (.a(a3), .b(b3), .s(s), .Out(outa3));
  mux1b2x1 mux1b2x1_3 (.a(a2), .b(b2), .s(s), .Out(outa2));
  mux1b2x1 mux1b2x1_4 (.a(a1), .b(b1), .s(s), .Out(outa1));
  mux1b2x1 mux1b2x1_5 (.a(a0), .b(b0), .s(s), .Out(outa0));
  mux1b2x1 mux1b2x1_6 (.a(cc), .b(dc), .s(s), .Out(outbc));
  mux1b2x1 mux1b2x1_7 (.a(c3), .b(d3), .s(s), .Out(outb3));
  mux1b2x1 mux1b2x1_8 (.a(c2), .b(d2), .s(s), .Out(outb2));
  mux1b2x1 mux1b2x1_9 (.a(c1), .b(d1), .s(s), .Out(outb1));
  mux1b2x1 mux1b2x1_10 (.a(c0), .b(d0), .s(s), .Out(outb0));
endmodule
